// Logisim project Pong.circ as structural Verilog: 5 circuits, main circuit main
module main (
  input  [7:0] _0,
  input  [7:0] _1,
  input  [7:0] _2,
  input  [7:0] _3,
  input  [7:0] _4,
  input  [7:0] _5,
  input  [7:0] _6,
  input  [7:0] _7,
  input  [7:0] _8,
  input  [7:0] _9,
  input  in_11,
  input  in_12,
  output [6:0] out_13
);

  wire button_1_out, clock_1_out, clock_2_out, counter_1_q, S1, S2, S3, S4, S5, S6, S7;
  wire [9:0] players_1_outp1, players_1_outp2;

  Button button_1 (.out(button_1_out));
  Clock clock_1 (.out(clock_1_out));
  Counter #(.width(1), .max('h1)) counter_1 (
    .count(button_1_out), .Q(counter_1_q), .clk(clock_1_out), .clr(counter_1_q));  // open: load, D, carry
  Keyboard keyboard_1 (.re(in_11), .clr(clock_2_out), .data(out_13));  // open: clk, avail
  Clock clock_2 (.out(clock_2_out));
  SEGMENTOS segmentos_1 (
    ._0(_0), ._1(_1), ._2(_2), ._3(_3), ._4(_4), ._5(_5), ._6(_6), ._7(_7), ._8(_8), ._9(_9),
    .CLOCK(counter_1_q), .out_14(S1), .out_15(S2), .out_16(S3), .out_17(S4), .out_18(S5), .out_19(S6),
    .out_20(S7), .ENABLE(in_12));  // open: reset, out_21
  _7_Segment_Display u_7_segment_display_1 (.g(S4), .f(S3), .a(S2), .b(S1), .e(S5), .d(S6), .c(S7));  // open: dp
  DotMatrix #(.matrixcols(20), .matrixrows(10)) dotmatrix_1 (
    .col0(players_1_outp1), .col19(players_1_outp2));  // open: col1, col2, col3, col4, col5, col6, col7, col8, col9, col10, col11, col12, col13, col14, col15, col16, col17, col18
  Players players_1 (.In(out_13), .OutP1(players_1_outp1), .OutP2(players_1_outp2));
endmodule

module Players (
  input  [6:0] In,
  output [9:0] OutP1,
  output [9:0] OutP2
);

  wire \direção_1_enable , \direção_1_out , \direção_2_enable , \direção_2_out , DownP1, DownP2, UpP1, UpP2;

  Comparator #(.width(7)) comparator_1 (.a(7'b1110111), .b(In), .eq(UpP1));  // open: gt, lt
  Comparator #(.width(7)) comparator_2 (.a(7'b1110011), .b(In), .eq(DownP1));  // open: gt, lt
  Comparator #(.width(7)) comparator_3 (.a(7'b1101111), .b(In), .eq(UpP2));  // open: gt, lt
  Comparator #(.width(7)) comparator_4 (.a(7'b1101100), .b(In), .eq(DownP2));  // open: gt, lt
  \Direção  \direção_1  (.Up_In(UpP1), .Down_In(DownP1), .Out(\direção_1_out ), .Enable(\direção_1_enable ));
  \Direção  \direção_2  (.Up_In(UpP2), .Down_In(DownP2), .Out(\direção_2_out ), .Enable(\direção_2_enable ));
  Movimento movimento_1 (.In(\direção_1_out ), .Enable(\direção_1_enable ), .Out(OutP1));
  Movimento movimento_2 (.In(\direção_2_out ), .Enable(\direção_2_enable ), .Out(OutP2));

  // Notes on the sheet:
  //   W
  //   S
  //   O
  //   L
endmodule

module \Direção  (
  input  Up_In,
  input  Down_In,
  output Out,
  output Enable
);

  wire and_1_out, xor_1_out;

  or or_1 (Enable, Up_In, Down_In);
  xor xor_1 (xor_1_out, Up_In, Down_In);
  and and_1 (and_1_out, Up_In, ~Down_In);  // AND_Gate
  and and_2 (Out, xor_1_out, and_1_out);
endmodule

module Movimento (
  input  In,
  input  Enable,
  output [9:0] Out
);

  wire and_3_out, clock_1_out, comparator_1_lt, comparator_2_lt, d_ff_1_q, not_1_out;
  wire [0:0] and_1_out, and_2_out;
  wire [9:0] multiplexer_1_out, multiplexer_2_out, multiplexer_3_out, shifter_1_out, shifter_2_out;

  Clock clock_1 (.out(clock_1_out));
  not not_1 (not_1_out, In);
  and and_1 (and_1_out[0], In, Enable);
  and and_2 (and_2_out[0], not_1_out, Enable);
  D_Flip_Flop d_ff_1 (.clk(clock_1_out), .D(clock_1_out), .Q(d_ff_1_q));  // open: Qn, preset, en, reset
  Multiplexer #(.width(10), .enable("false")) multiplexer_1 (
    .in0(multiplexer_2_out), .in1(Out), .out(multiplexer_1_out), .sel(and_2_out[0]));
  Multiplexer #(.width(10), .enable("false")) multiplexer_2 (
    .in0(10'hf), .in1(Out), .out(multiplexer_2_out), .sel(d_ff_1_q));
  Shifter #(.width(10), .shift("lr")) shifter_1 (
    .in(multiplexer_1_out), .\dist ({3'b000, and_2_out[0]}), .out(shifter_1_out));
  Multiplexer #(.width(10), .enable("false")) multiplexer_3 (
    .in0(shifter_1_out), .in1(shifter_2_out), .out(multiplexer_3_out), .sel(and_1_out[0]));
  Shifter #(.width(10)) shifter_2 (.in(multiplexer_2_out), .\dist ({3'b000, and_1_out[0]}), .out(shifter_2_out));
  Comparator #(.width(10)) comparator_1 (.a(10'h7), .b(shifter_1_out), .lt(comparator_1_lt));  // open: gt, eq
  Comparator #(.width(10)) comparator_2 (.a(10'h380), .b(shifter_2_out), .lt(comparator_2_lt));  // open: gt, eq
  and and_3 (and_3_out, comparator_1_lt, comparator_2_lt);
  Register #(.width(10)) register_1 (.D(multiplexer_3_out), .en(and_3_out), .Q(Out), .clk(clock_1_out));  // open: clr
endmodule

module SEGMENTOS (
  input  [7:0] _0,
  input  [7:0] _1,
  input  [7:0] _2,
  input  [7:0] _3,
  input  [7:0] _4,
  input  [7:0] _5,
  input  [7:0] _6,
  input  [7:0] _7,
  input  [7:0] _8,
  input  [7:0] _9,
  input  ENABLE,
  input  CLOCK,
  input  reset,
  output out_14,
  output out_15,
  output out_16,
  output out_17,
  output out_18,
  output out_19,
  output out_20,
  output out_21
);

  wire and_1_out, or_1_out;
  wire [3:0] counter_1_q, multiplexer_2_out;

  Counter #(.width(4), .max('hf)) counter_1 (
    .count(CLOCK), .Q(counter_1_q), .clk(CLOCK), .clr(or_1_out));  // open: load, D, carry
  or or_1 (or_1_out, reset, and_1_out);
  Multiplexer #(.select(4), .width(8)) multiplexer_1 (
    .in0(_0), .in1(_1), .in2(_2), .in3(_3), .in4(_4), .in5(_5), .in6(_6), .in7(_7), .in8(_8), .in9(_9),
    .out({out_21, out_20, out_19, out_18, out_17, out_16, out_15, out_14}), .sel(counter_1_q), .en(ENABLE));  // open: in10, in11, in12, in13, in14, in15
  Multiplexer #(.select(4), .width(4)) multiplexer_2 (
    .in10(counter_1_q), .out(multiplexer_2_out), .sel(counter_1_q), .en(ENABLE));  // open: in0, in1, in2, in3, in4, in5, in6, in7, in8, in9, in11, in12, in13, in14, in15
  and and_1 (and_1_out, ~multiplexer_2_out[0], multiplexer_2_out[1], ~multiplexer_2_out[2], multiplexer_2_out[3]);  // AND_Gate
endmodule
